# Fritzing sketch pythagotron (saved by Fritzing 0.9.1b)
circuit board: 9.5cm x 4.9cm
breadboards: 3

parts:
  StpOut1 = female pin header, 4 pins [form="♀ (female)"]
  Power_plug1 = Power plug
  StpOut2 = female pin header, 4 pins [form="♀ (female)"]
  SrvOut2 = female pin header, 3 pins [form="♀ (female)"]
  SrvOu1 = female pin header, 3 pins [form="♀ (female)"]
  DCconvOut = female pin header, 2 pins [form="♀ (female)"]
  DCconvIn = female pin header, 2 pins [form="♀ (female)"]
  Q1 = Basic FET N-Channel [package="TO220 [THT]"]
  Q2 = Basic FET N-Channel [package="TO220 [THT]"]
  DIn1 = female pin header, 2 pins [form="♀ (female)"]
  MosOut2 = female pin header, 2 pins [form="♀ (female)"]
  MosOut1 = female pin header, 2 pins [form="♀ (female)"]
  DIn2 = female pin header, 2 pins [form="♀ (female)"]
  AIn1 = female pin header, 3 pins [form="♀ (female)"]
  AIn2 = female pin header, 3 pins [form="♀ (female)"]
  SJ1 = female pin header, 3 pins [form="♀ (female)"]
  SJ2 = female pin header, 3 pins [form="♀ (female)"]
  pull1 = female pin header, 2 pins [form="♀ (female)"]
  pull2 = female pin header, 2 pins [form="♀ (female)"]
  Pololu_A2 = Pololu A4988 [package=SO16]
  Pololu_A1 = Pololu A4988 [package=SO16]
  Part1 = Arduino Nano (Rev3.0)
  U2 = Optocoupler [package=THT]
  R1 = Resistor [tolerance=±5% resistance=220 package=THT]
  D1 = Rectifier Diode [part_number=1N4001 package="300 mil [THT]"]
  R2 = Resistor [tolerance=±5% resistance=1k package=THT]
  R3 = Resistor [tolerance=±5% resistance=100k package=THT]
  R4 = Resistor [tolerance=±5% resistance=100k package=THT]
  R5 = Resistor [tolerance=±5% resistance=100 package=THT]
  R6 = Resistor [tolerance=±5% resistance=100 package=THT]
  C1 = Electrolytic Capacitor [capacitance=47µF voltage=20V package="100 mil [THT, electrolytic]"]
  C2 = Electrolytic Capacitor [capacitance=47µF voltage=20V package="100 mil [THT, electrolytic]"]
  D2 = Rectifier Diode [part_number=1N4001 package="300 mil [THT]"]
  D3 = Rectifier Diode [part_number=1N4001 package="300 mil [THT]"]
  U4 = MIDI_CONN_FEMALE [package=din_5_female]

nets:
  N1: StpOut1.pin1, Pololu_A1.1B
  N2: StpOut1.pin2, Pololu_A1.1A
  N3: StpOut1.pin3, Pololu_A1.2A
  N4: StpOut1.pin4, Pololu_A1.2B
  GND: Power_plug1.GND, SrvOut2.pin3, SrvOu1.pin3, DCconvOut.pin2, DCconvIn.pin2, Q1.source, Q2.source, DIn1.pin1, DIn2.pin1, AIn1.pin1, AIn2.pin1, pull1.pin2, pull2.pin2, Pololu_A2.GND, Pololu_A1.GND, Part1.GND, U2.Pin_4, R3.Pin_0, R4.Pin_0, C1.-, C2.-
  N5: Power_plug1.VCC, DCconvIn.pin1, MosOut2.pin2, MosOut1.pin2, Pololu_A2.VMOT, Pololu_A1.VMOT, C2.+, D2.cathode, D3.cathode
  N6: StpOut2.pin1, Pololu_A2.1B
  N7: StpOut2.pin2, Pololu_A2.1A
  N8: StpOut2.pin3, Pololu_A2.2A
  N9: StpOut2.pin4, Pololu_A2.2B
  N10: SrvOut2.pin1, Part1.D9
  N11: SrvOut2.pin2, SrvOu1.pin2, DCconvOut.pin1, Part1.VIN, C1.+
  N12: SrvOu1.pin1, Part1.D8
  N13: Q1.gate, R4.Pin_1, R6.Pin_0
  N14: Q1.drain, MosOut2.pin1, D3.anode
  N15: Q2.gate, R3.Pin_1, R5.Pin_0
  N16: Q2.drain, MosOut1.pin1, D2.anode
  N17: DIn1.pin2, Part1.D13/SCK
  N18: DIn2.pin2, Part1.D12/MISO
  N19: AIn1.pin2, Part1.A7
  VDD: AIn1.pin3, AIn2.pin3, pull1.pin1, pull2.pin1, Pololu_A2.VDD, Pololu_A1.VDD, Part1.5V, R2.Pin_0
  N20: AIn2.pin2, Part1.A6
  N21: SJ1.pin1, Pololu_A1.MS1
  N22: SJ1.pin2, Pololu_A1.MS2
  N23: SJ1.pin3, Pololu_A1.MS3
  N24: SJ2.pin1, Pololu_A2.MS1
  N25: SJ2.pin2, Pololu_A2.MS2
  N26: SJ2.pin3, Pololu_A2.MS3
  N27: Pololu_A2.ENABLE, Part1.D7
  N28: Pololu_A2.RESET, Pololu_A2.SLEEP
  N29: Pololu_A2.STEP, Part1.D6
  N30: Pololu_A2.DIR, Part1.D5
  N31: Pololu_A1.ENABLE, Part1.D4
  N32: Pololu_A1.RESET, Pololu_A1.SLEEP
  N33: Pololu_A1.STEP, Part1.D3
  N34: Pololu_A1.DIR, Part1.D2
  N35: Part1.D0/RX, U2.Pin_5, R2.Pin_1
  N36: Part1.D10, R6.Pin_1
  N37: Part1.D11/MOSI, R5.Pin_1
  N38: U2.Pin_1, R1.Pin_1
  N39: U2.Pin_2, D1.anode, U4.MIDI_IN
  N40: R1.Pin_0, D1.cathode, U4.MIDI_OUT
