# Fritzing sketch mainboard (saved by Fritzing 0.9.2b)
circuit board: 9.7cm x 4.9cm
breadboards: 2

parts:
  DCconvOut = female pin header, 2 pins [form="♀ (female)"]
  Q1 = Basic FET N-Channel [package="TO220 [THT]"]
  DIn2 = female pin header, 2 pins [form="♀ (female)"]
  SrvOut2 = female pin header, 3 pins [form="♀ (female)"]
  D2 = Rectifier Diode [part_number=1N4001 package="300 mil [THT]"]
  AIn1 = female pin header, 3 pins [form="♀ (female)"]
  StpOut2 = female pin header, 4 pins [form="♀ (female)"]
  R4 = Resistor [tolerance=±5% resistance=100k package=THT]
  Q2 = Basic FET N-Channel [package="TO220 [THT]"]
  SJ1 = female pin header, 3 pins [form="♀ (female)"]
  pull2 = female pin header, 2 pins [form="♀ (female)"]
  SrvOu1 = female pin header, 3 pins [form="♀ (female)"]
  MosOut1 = female pin header, 2 pins [form="♀ (female)"]
  DCconvIn = female pin header, 2 pins [form="♀ (female)"]
  SJ2 = female pin header, 3 pins [form="♀ (female)"]
  Power_plug1 = Power plug
  R5 = Resistor [tolerance=±5% resistance=100 package=THT]
  MosOut2 = female pin header, 2 pins [form="♀ (female)"]
  D3 = Rectifier Diode [part_number=1N4001 package="300 mil [THT]"]
  Pololu_A1 = Pololu A4988 [package=SO16]
  pull1 = female pin header, 2 pins [form="♀ (female)"]
  StpOut1 = female pin header, 4 pins [form="♀ (female)"]
  DIn1 = female pin header, 2 pins [form="♀ (female)"]
  R3 = Resistor [tolerance=±5% resistance=100k package=THT]
  R6 = Resistor [tolerance=±5% resistance=100 package=THT]
  AIn2 = female pin header, 3 pins [form="♀ (female)"]
  Part1 = Arduino Nano (Rev3.0)
  Pololu_A2 = Pololu A4988 [package=SO16]
  Pad1 = Pad [width=48 height=23 connect=center]  # not connected

nets:
  N1: DCconvOut.pin1, SrvOut2.pin2, SrvOu1.pin2
  GND: DCconvOut.pin2, Q1.source, DIn2.pin1, SrvOut2.pin3, AIn1.pin1, R4.Pin_0, Q2.source, pull2.pin2, SrvOu1.pin3, DCconvIn.pin2, Power_plug1.GND, Pololu_A1.GND, pull1.pin2, DIn1.pin1, R3.Pin_0, AIn2.pin1, Part1.GND, Pololu_A2.GND
  N2: Q1.gate, R4.Pin_1, R6.Pin_0
  N3: Q1.drain, MosOut2.pin1, D3.anode
  N4: DIn2.pin2, Part1.D12/MISO
  N5: SrvOut2.pin1, Part1.D9
  VCC: D2.cathode, MosOut1.pin2, DCconvIn.pin1, Power_plug1.VCC, MosOut2.pin2, D3.cathode, Pololu_A1.VMOT, Part1.VIN, Pololu_A2.VMOT
  N6: D2.anode, Q2.drain, MosOut1.pin1
  N7: AIn1.pin2, Part1.A0
  VDD: AIn1.pin3, pull2.pin1, Pololu_A1.VDD, pull1.pin1, AIn2.pin3, Part1.5V, Pololu_A2.VDD
  N8: StpOut2.pin1, Pololu_A2.1B
  N9: StpOut2.pin2, Pololu_A2.1A
  N10: StpOut2.pin3, Pololu_A2.2A
  N11: StpOut2.pin4, Pololu_A2.2B
  N12: Q2.gate, R5.Pin_0, R3.Pin_1
  N13: SJ1.pin1, Pololu_A1.MS1
  N14: SJ1.pin2, Pololu_A1.MS2
  N15: SJ1.pin3, Pololu_A1.MS3
  N16: SrvOu1.pin1, Part1.D8
  N17: SJ2.pin1, Pololu_A2.MS1
  N18: SJ2.pin2, Pololu_A2.MS2
  N19: SJ2.pin3, Pololu_A2.MS3
  N20: R5.Pin_1, Part1.D11/MOSI
  N21: Pololu_A1.ENABLE, Part1.D2
  N22: Pololu_A1.RESET, Pololu_A1.SLEEP
  N23: Pololu_A1.STEP, Part1.D3
  N24: Pololu_A1.DIR, Part1.D4
  N25: Pololu_A1.1B, StpOut1.pin1
  N26: Pololu_A1.1A, StpOut1.pin2
  N27: Pololu_A1.2A, StpOut1.pin3
  N28: Pololu_A1.2B, StpOut1.pin4
  N29: DIn1.pin2, Part1.D13/SCK
  N30: R6.Pin_1, Part1.D10
  N31: AIn2.pin2, Part1.A1
  N32: Part1.D5, Pololu_A2.ENABLE
  N33: Part1.D6, Pololu_A2.STEP
  N34: Part1.D7, Pololu_A2.DIR
  N35: Pololu_A2.RESET, Pololu_A2.SLEEP
