# Fritzing sketch piezo_preamp (saved by Fritzing 0.9.2b)
circuit board: 2.94457cm x 4.33722cm
breadboards: 1

parts:
  IC1 = tl081 [chip_label=IC package="DIP (Dual Inline) [THT]"]
  J1 = female pin header, 2 pins [form="♀ (female)"]
  J2 = female pin header, 2 pins [form="♀ (female)"]
  J3 = female pin header, 2 pins [form="♀ (female)"]
  R1 = Resistor [tolerance=±5% resistance=470k package=THT]
  R2 = Resistor [tolerance=±20% resistance=220 package=THT]
  R3 = Resistor [tolerance=±5% resistance=1M package=THT]
  R4 = Resistor [tolerance=±5% resistance=470k package=THT]
  C2 = Electrolytic Capacitor [capacitance=10µF voltage=16V package="100 mil [THT, electrolytic]"]
  C1 = Ceramic Capacitor [capacitance=10nF package="100 mil [THT, multilayer]"]
  D1 = Diode [package=diode-1n4148]
  R5 = TRIMPOT [package=trimpot_pth_s3_lock]

nets:
  N1: IC1.in-, J2.pin1, R3.Pin_1, C1.1
  N2: IC1.in+, R1.Pin_1, R4.Pin_0
  N3: IC1.out, R2.Pin_1, R3.Pin_0, C1.0
  N4: IC1.vcc+, J1.pin2, R4.Pin_1
  N5: J1.pin1, D1.C
  N6: J3.pin2, R5.WIPER
  N7: R2.Pin_0, C2.+
  N8: C2.-, R5.CW
